# Fritzing sketch Wiring (saved by Fritzing 0.9.3b)
breadboards: 4

parts:
  Part1 = Arduino Mega 2560 (Rev3)
  Part2 = LCD1602-I2C
  S1 = KY-026
  J1 = Basic Servo
  Part4 = RFID-RC522-v2
  HC-SR04_Sensor_1 = HC-SR04 Ultrasonic Distance Sensor
  Matrix_keypad1 = KEYPAD 4x4
  LED1 = 8x8 LED Matrix (blue)
  M1 = fc-51 [package=THT]
  A1 = uhppote electric strike door lock
  M2 = 1 chan 5v relay module
  HLK-PM1 = HLK-PM12 [part_number=HLK-PM12]
  PIR1 = PIR sensor
  LED2 = 8x8 LED Matrix (blue)
  M3 = fc-51 [package=THT]
  A2 = uhppote electric strike door lock
  M4 = 1 chan 5v relay module
  PIR2 = PIR sensor
  Matrix_keypad2 = KEYPAD 4x4
  HC-SR04_Sensor_2 = HC-SR04 Ultrasonic Distance Sensor
  Part6 = LCD1602-I2C
  S2 = KY-026
  J2 = Basic Servo
  Part8 = RFID-RC522-v2
  Raspberry_Pi_1 = Raspberry Pi 4 [part_number=RPI-4-b]

nets:
  N1: Part1.A0, S1.pin1
  N2: Part1.SCL, Part2.SCL
  N3: Part1.SDA, Part2.SDA
  N4: Part1.D13_PWM, M1.pin1
  N5: Part1.D9_PWM, Part4.SDA
  N6: Part1.D8_PWM, Part4.RST
  3V3: Part1.3V3, Part4.3.3V
  GND: Part1.GND, Part4.GND
  N7: Part1.D2_PWM, J1.pulse
  N8: Part1.D6_PWM, HC-SR04_Sensor_1.ECHO
  N9: Part1.D7_PWM, HC-SR04_Sensor_1.TRIG
  N10: Part1.D22, S1.pin4
  N11: Part1.D23, PIR1.SIG
  N12: Part1.D24, M2.pin_3
  N13: Part1.D29, Matrix_keypad1.col1
  N14: Part1.D31, Matrix_keypad1.col2
  N15: Part1.D33, Matrix_keypad1.col3
  N16: Part1.D35, Matrix_keypad1.col4
  N17: Part1.D37, Matrix_keypad1.row1
  N18: Part1.D39, Matrix_keypad1.row2
  N19: Part1.D41, Matrix_keypad1.row3
  N20: Part1.D43, Matrix_keypad1.row4
  N21: Part1.D50, Part4.MOSI
  N22: Part1.D51, Part4.MISO, LED1.D
  N23: Part1.D52, Part4.SCK, LED1.C
  GND_2: Part2.GND, S1.pin2, J1.gnd, HC-SR04_Sensor_1.GND
  VCC: Part2.VCC, S1.pin3, J1.vcc, HC-SR04_Sensor_1.VCC
  N24: LED1.+, PIR1.VDD
  N25: LED1.-, M1.pin2, M1.pin3, PIR1.GND
  N26: A1.pin1, M2.pin_5
  N27: A1.pin2, HLK-PM1.-Vo, A2.pin2
  N28: M2.pin_6, HLK-PM1.+Vo, M4.pin_4
  N29: LED2.+, PIR2.VDD
  N30: LED2.-, M3.pin2, M3.pin3, PIR2.GND
  N31: LED2.C, Part8.MOSI, Raspberry_Pi_1.GPIO10
  N32: M3.pin1, Raspberry_Pi_1.GPIO21
  N33: A2.pin1, M4.pin_5
  N34: M4.pin_3, Raspberry_Pi_1.GPIO13
  N35: PIR2.SIG, Raspberry_Pi_1.GPIO12
  N36: Matrix_keypad2.col1, Raspberry_Pi_1.GPIO4
  N37: Matrix_keypad2.col2, Raspberry_Pi_1.GPIO5
  N38: Matrix_keypad2.col3, Raspberry_Pi_1.GPIO6
  N39: Matrix_keypad2.col4, Raspberry_Pi_1.GPIO26
  N40: Matrix_keypad2.row1, Raspberry_Pi_1.GPIO22
  N41: Matrix_keypad2.row2, Raspberry_Pi_1.GPIO23
  N42: Matrix_keypad2.row3, Raspberry_Pi_1.GPIO24
  N43: Matrix_keypad2.row4, Raspberry_Pi_1.GPIO27
  VCC_2: HC-SR04_Sensor_2.VCC, Part6.VCC, S2.pin3, J2.vcc
  N44: HC-SR04_Sensor_2.TRIG, Raspberry_Pi_1.GPIO16
  N45: HC-SR04_Sensor_2.ECHO, Raspberry_Pi_1.GPIO20
  GND_3: HC-SR04_Sensor_2.GND, Part6.GND, S2.pin2, J2.gnd
  N46: Part6.SDA, Part8.SDA, Raspberry_Pi_1.GPIO2, Raspberry_Pi_1.5V
  N47: Part6.SCL, Raspberry_Pi_1.GPIO3
  N48: S2.pin4, Raspberry_Pi_1.GPIO17
  N49: Part8.SCK, Raspberry_Pi_1.GPIO11
  N50: Part8.MISO, Raspberry_Pi_1.GPIO9

custom parts:
  LCD1602-I2C: A standard character display, usually with 2x16 characters. Comes in many colors with LCM1602 IIC attached.
  KY-026: ky-026 flame sensor module
  RFID-RC522-v2: A simple China made RFID-RC522 Reader; do check the pin labels, as this is a MFRC522 based clone.
  KEYPAD 4x4: Matrix keypad 16 buttons, 4 rows x 4 columns
  8x8 LED Matrix (blue): 8x8 LED Matrix with I2C control (blue)
  uhppote electric strike door lock: UHPPOTE electric strike door lock.
  1 chan 5v relay module: 1 Channel 5V Relay Module Board Shield with Optocoupler Support High and Low Level Trigger for Arduino.
  Raspberry Pi 4: The RPi4, a faster version of the awesome Raspberry Pi 2 B ARM Board with 40 pin gpio. Ready for special Raspberry Pi B+ and RPi2 Hat (Hardware attached (on) top)
